// Logisim project 32bitALU.circ as structural Verilog
module main (
  input  [1:0] in_1,
  input  in_2,
  input  [31:0] Instruction
);

  wire ALUOp1, ALUOp2, ALUSrc, and_1_out, Branch, clock_1_out, clock_2_out, clock_3_out, Jump, MemRead,
       MemtoReg, MemWrite, RegDst, RegWrite, Zero;
  wire [3:0] ALUCtl;
  wire [4:0] multiplexer_1_out;
  wire [27:0] PC_plus4;
  wire [31:0] adder_2_out, alu_32_1_result, multiplexer_2_out, multiplexer_3_out, PC_data, PC_dataout,
       ram_1_dout, RegisterData, registergroup_1_dataout1, registergroup_1_dataout2;
  wire [31:2] BranchOffset;
  wire [31:28] JumpAddress;
  wire [31:30] SignExtend;

  // Probe on Instruction[15:11]
  // Probe on Instruction[25:21]
  assign {SignExtend, BranchOffset} = {{16{Instruction[15]}}, Instruction[15:0]};  // Bit_Extender bit_extender_1
  // Probe on Instruction[20:16]
  Clock clock_1 (.out(clock_1_out));
  ControlUnit controlunit_1 (
    .Op5(Instruction[31]), .Op4(Instruction[30]), .Op3(Instruction[29]), .Op2(Instruction[28]),
    .Op1(Instruction[27]), .Op0(Instruction[26]), .RegDst(RegDst), .ALUSrc(ALUSrc), .MemtoReg(MemtoReg),
    .RegWrite(RegWrite), .MemRead(MemRead), .MemWrite(MemWrite), .Branch(Branch), .ALUOp1(ALUOp1),
    .ALUOp0(ALUOp2), .Jump(Jump));
  Multiplexer #(.width(5)) multiplexer_1 (
    .in0(Instruction[20:16]), .in1(Instruction[15:11]), .out(multiplexer_1_out), .sel(RegDst));
  // Probe on Instruction[5:0]
  // Probe on RegisterData
  ALUControl alucontrol_1 (.FUNCT(Instruction[5:0]), .OP1(ALUOp1), .OP2(ALUOp2), .out_4(ALUCtl));
  Clock clock_2 (.out(clock_2_out));
  // Probe on registergroup_1_dataout2
  RegisterGroup registergroup_1 (
    .Data(RegisterData), .write(RegWrite), .clock(clock_1_out), .Sel1_ReadReg1(Instruction[25:21]),
    .Sel2_ReadReg2(Instruction[20:16]), .RegNum_WriteReg(multiplexer_1_out),
    .DataOut1(registergroup_1_dataout1), .DataOut2(registergroup_1_dataout2));
  // Probe on registergroup_1_dataout1
  Multiplexer #(.width(32)) multiplexer_2 (
    .in0(registergroup_1_dataout2), .in1({SignExtend, BranchOffset}), .out(multiplexer_2_out), .sel(ALUSrc));
  ALU_32 alu_32_1 (
    .A(registergroup_1_dataout1), .B(multiplexer_2_out), .Control(ALUCtl), .Cin(ALUCtl[2]), .Zero(Zero),
    .Result(alu_32_1_result));  // open: Cout, Negative, Overflow
  Registr PC (.data(PC_data), .clk(clock_2_out), .Reset(in_2), .DataOut(PC_dataout));
  // Probe on ALUCtl
  // Probe on alu_32_1_result
  Clock clock_3 (.out(clock_3_out));
  // Probe on {JumpAddress, Instruction[25:0], in_1}
  Adder #(.width(32)) adder_1 (.a(PC_dataout), .b(32'h4), .out({JumpAddress, PC_plus4}));  // open: cin, cout
  RAM #(.dataWidth(32)) ram_1 (
    .addr(alu_32_1_result[7:0]), .we(MemWrite), .oe(MemRead), .clk(clock_3_out),
    .din(registergroup_1_dataout2), .dout(ram_1_dout));
  Adder #(.width(32)) adder_2 (
    .a({JumpAddress, PC_plus4}), .b({BranchOffset, 2'b00}), .out(adder_2_out));  // open: cin, cout
  and and_1 (and_1_out, Branch, Zero);
  Multiplexer #(.width(32)) multiplexer_3 (
    .in0({JumpAddress, PC_plus4}), .in1(adder_2_out), .out(multiplexer_3_out), .sel(and_1_out));
  Multiplexer #(.width(32)) multiplexer_4 (.in0(alu_32_1_result), .in1(ram_1_dout), .out(RegisterData), .sel(MemtoReg));
  // Probe on PC_data
  Multiplexer #(.width(32)) multiplexer_5 (
    .in0(multiplexer_3_out), .in1({JumpAddress, Instruction[25:0], in_1}), .out(PC_data), .sel(Jump));

  // Other names for the same wires on the sheet: JumpAddress[27:0] = {Instruction[25:0], in_1};
  //   Funct[5:0] = Instruction[5:0]; JumpTarget[25:0] = Instruction[25:0]; PC_plus4[31:28] = JumpAddress;
  //   SignExtend[29:0] = BranchOffset
endmodule

module OneBitALU (
  input  Cin,
  input  A,
  input  B,
  input  [3:0] ALU_Control,
  input  Less,
  output Result,
  output Cout,
  output Set
);

  wire and_1_out, multiplexer_1_out, multiplexer_2_out, not_1_out, not_2_out, or_1_out;

  not not_1 (not_1_out, A);
  not not_2 (not_2_out, B);
  Multiplexer multiplexer_1 (.in0(A), .in1(not_1_out), .out(multiplexer_1_out), .sel(ALU_Control[3]));
  Multiplexer multiplexer_2 (.in0(B), .in1(not_2_out), .out(multiplexer_2_out), .sel(ALU_Control[2]));
  Adder #(.width(1)) adder_1 (.a(multiplexer_1_out), .b(multiplexer_2_out), .out(Set), .cin(Cin), .cout(Cout));
  and and_1 (and_1_out, multiplexer_1_out, multiplexer_2_out);
  or or_1 (or_1_out, multiplexer_1_out, multiplexer_2_out);
  Multiplexer #(.select(2)) multiplexer_3 (
    .in0(and_1_out), .in1(or_1_out), .in2(Set), .in3(Less), .out(Result), .sel(ALU_Control[1:0]));
endmodule

module ALU_32 (
  input  [31:0] A,
  input  Cin,
  input  [3:0] Control,
  input  [31:0] B,
  output Cout,
  output Overflow,
  output Zero,
  output Negative,
  output [31:0] Result
);

  wire and_1_out, and_2_out, not_1_out, not_2_out, not_3_out, onebitalu_1_cout, onebitalu_2_cout,
       onebitalu_3_cout, onebitalu_4_cout, onebitalu_5_cout, onebitalu_6_cout, onebitalu_7_cout,
       onebitalu_8_cout, onebitalu_9_cout, onebitalu_10_cout, onebitalu_11_cout, onebitalu_12_cout,
       onebitalu_13_cout, onebitalu_14_cout, onebitalu_15_cout, onebitalu_16_cout, onebitalu_17_cout,
       onebitalu_18_cout, onebitalu_19_cout, onebitalu_20_cout, onebitalu_21_cout, onebitalu_22_cout,
       onebitalu_23_cout, onebitalu_24_cout, onebitalu_25_cout, onebitalu_26_cout, onebitalu_27_cout,
       onebitalu_28_cout, onebitalu_29_cout, onebitalu_30_cout, onebitalu_31_cout, onebitalu_32_set, or_2_out;

  not not_1 (not_1_out, A[31]);
  not not_2 (not_2_out, B[31]);
  not not_3 (not_3_out, Negative);
  and and_1 (and_1_out, not_1_out, not_2_out, Negative);
  and and_2 (and_2_out, A[31], B[31], not_3_out);
  or or_1 (Overflow, and_1_out, and_2_out);
  OneBitALU onebitalu_1 (
    .Cin(Cin), .A(A[0]), .B(B[0]), .ALU_Control(Control), .Less(onebitalu_32_set), .Result(Result[0]),
    .Cout(onebitalu_1_cout));  // open: Set
  OneBitALU onebitalu_2 (
    .Cin(onebitalu_1_cout), .A(A[1]), .B(B[1]), .ALU_Control(Control), .Less(1'b0), .Result(Result[1]),
    .Cout(onebitalu_2_cout));  // open: Set
  OneBitALU onebitalu_3 (
    .Cin(onebitalu_2_cout), .A(A[2]), .B(B[2]), .ALU_Control(Control), .Less(1'b0), .Result(Result[2]),
    .Cout(onebitalu_3_cout));  // open: Set
  OneBitALU onebitalu_4 (
    .Cin(onebitalu_3_cout), .A(A[3]), .B(B[3]), .ALU_Control(Control), .Less(1'b0), .Result(Result[3]),
    .Cout(onebitalu_4_cout));  // open: Set
  OneBitALU onebitalu_5 (
    .Cin(onebitalu_4_cout), .A(A[4]), .B(B[4]), .ALU_Control(Control), .Less(1'b0), .Result(Result[4]),
    .Cout(onebitalu_5_cout));  // open: Set
  OneBitALU onebitalu_6 (
    .Cin(onebitalu_5_cout), .A(A[5]), .B(B[5]), .ALU_Control(Control), .Less(1'b0), .Result(Result[5]),
    .Cout(onebitalu_6_cout));  // open: Set
  OneBitALU onebitalu_7 (
    .Cin(onebitalu_6_cout), .A(A[6]), .B(B[6]), .ALU_Control(Control), .Less(1'b0), .Result(Result[6]),
    .Cout(onebitalu_7_cout));  // open: Set
  OneBitALU onebitalu_8 (
    .Cin(onebitalu_7_cout), .A(A[7]), .B(B[7]), .ALU_Control(Control), .Less(1'b0), .Result(Result[7]),
    .Cout(onebitalu_8_cout));  // open: Set
  OneBitALU onebitalu_9 (
    .Cin(onebitalu_8_cout), .A(A[8]), .B(B[8]), .ALU_Control(Control), .Less(1'b0), .Result(Result[8]),
    .Cout(onebitalu_9_cout));  // open: Set
  OneBitALU onebitalu_10 (
    .Cin(onebitalu_9_cout), .A(A[9]), .B(B[9]), .ALU_Control(Control), .Less(1'b0), .Result(Result[9]),
    .Cout(onebitalu_10_cout));  // open: Set
  OneBitALU onebitalu_11 (
    .Cin(onebitalu_10_cout), .A(A[10]), .B(B[10]), .ALU_Control(Control), .Less(1'b0), .Result(Result[10]),
    .Cout(onebitalu_11_cout));  // open: Set
  OneBitALU onebitalu_12 (
    .Cin(onebitalu_11_cout), .A(A[11]), .B(B[11]), .ALU_Control(Control), .Less(1'b0), .Result(Result[11]),
    .Cout(onebitalu_12_cout));  // open: Set
  OneBitALU onebitalu_13 (
    .Cin(onebitalu_12_cout), .A(A[12]), .B(B[12]), .ALU_Control(Control), .Less(1'b0), .Result(Result[12]),
    .Cout(onebitalu_13_cout));  // open: Set
  OneBitALU onebitalu_14 (
    .Cin(onebitalu_13_cout), .A(A[13]), .B(B[13]), .ALU_Control(Control), .Less(1'b0), .Result(Result[13]),
    .Cout(onebitalu_14_cout));  // open: Set
  OneBitALU onebitalu_15 (
    .Cin(onebitalu_14_cout), .A(A[14]), .B(B[14]), .ALU_Control(Control), .Less(1'b0), .Result(Result[14]),
    .Cout(onebitalu_15_cout));  // open: Set
  OneBitALU onebitalu_16 (
    .Cin(onebitalu_15_cout), .A(A[15]), .B(B[15]), .ALU_Control(Control), .Less(1'b0), .Result(Result[15]),
    .Cout(onebitalu_16_cout));  // open: Set
  OneBitALU onebitalu_17 (
    .Cin(onebitalu_16_cout), .A(A[16]), .B(B[16]), .ALU_Control(Control), .Less(1'b0), .Result(Result[16]),
    .Cout(onebitalu_17_cout));  // open: Set
  OneBitALU onebitalu_18 (
    .Cin(onebitalu_17_cout), .A(A[17]), .B(B[17]), .ALU_Control(Control), .Less(1'b0), .Result(Result[17]),
    .Cout(onebitalu_18_cout));  // open: Set
  OneBitALU onebitalu_19 (
    .Cin(onebitalu_18_cout), .A(A[18]), .B(B[18]), .ALU_Control(Control), .Less(1'b0), .Result(Result[18]),
    .Cout(onebitalu_19_cout));  // open: Set
  OneBitALU onebitalu_20 (
    .Cin(onebitalu_19_cout), .A(A[19]), .B(B[19]), .ALU_Control(Control), .Less(1'b0), .Result(Result[19]),
    .Cout(onebitalu_20_cout));  // open: Set
  OneBitALU onebitalu_21 (
    .Cin(onebitalu_20_cout), .A(A[20]), .B(B[20]), .ALU_Control(Control), .Less(1'b0), .Result(Result[20]),
    .Cout(onebitalu_21_cout));  // open: Set
  OneBitALU onebitalu_22 (
    .Cin(onebitalu_21_cout), .A(A[21]), .B(B[21]), .ALU_Control(Control), .Less(1'b0), .Result(Result[21]),
    .Cout(onebitalu_22_cout));  // open: Set
  OneBitALU onebitalu_23 (
    .Cin(onebitalu_22_cout), .A(A[22]), .B(B[22]), .ALU_Control(Control), .Less(1'b0), .Result(Result[22]),
    .Cout(onebitalu_23_cout));  // open: Set
  OneBitALU onebitalu_24 (
    .Cin(onebitalu_23_cout), .A(A[23]), .B(B[23]), .ALU_Control(Control), .Less(1'b0), .Result(Result[23]),
    .Cout(onebitalu_24_cout));  // open: Set
  OneBitALU onebitalu_25 (
    .Cin(onebitalu_24_cout), .A(A[24]), .B(B[24]), .ALU_Control(Control), .Less(1'b0), .Result(Result[24]),
    .Cout(onebitalu_25_cout));  // open: Set
  OneBitALU onebitalu_26 (
    .Cin(onebitalu_25_cout), .A(A[25]), .B(B[25]), .ALU_Control(Control), .Less(1'b0), .Result(Result[25]),
    .Cout(onebitalu_26_cout));  // open: Set
  OneBitALU onebitalu_27 (
    .Cin(onebitalu_26_cout), .A(A[26]), .B(B[26]), .ALU_Control(Control), .Less(1'b0), .Result(Result[26]),
    .Cout(onebitalu_27_cout));  // open: Set
  OneBitALU onebitalu_28 (
    .Cin(onebitalu_27_cout), .A(A[27]), .B(B[27]), .ALU_Control(Control), .Less(1'b0), .Result(Result[27]),
    .Cout(onebitalu_28_cout));  // open: Set
  OneBitALU onebitalu_29 (
    .Cin(onebitalu_28_cout), .A(A[28]), .B(B[28]), .ALU_Control(Control), .Less(1'b0), .Result(Result[28]),
    .Cout(onebitalu_29_cout));  // open: Set
  OneBitALU onebitalu_30 (
    .Cin(onebitalu_29_cout), .A(A[29]), .B(B[29]), .ALU_Control(Control), .Less(1'b0), .Result(Result[29]),
    .Cout(onebitalu_30_cout));  // open: Set
  OneBitALU onebitalu_31 (
    .Cin(onebitalu_30_cout), .A(A[30]), .B(B[30]), .ALU_Control(Control), .Less(1'b0), .Result(Result[30]),
    .Cout(onebitalu_31_cout));  // open: Set
  OneBitALU onebitalu_32 (
    .Cin(onebitalu_31_cout), .A(A[31]), .B(B[31]), .ALU_Control(Control), .Less(1'b0), .Result(Negative),
    .Cout(Cout), .Set(onebitalu_32_set));
  or or_2 (or_2_out, Result[0], Result[1], Result[2], Result[3], Result[4], Result[5], Result[6], Result[7], Result[8], Result[9], Result[10], Result[11], Result[12], Result[13], Result[14], Result[15], Result[16], Result[17], Result[18], Result[19], Result[20], Result[21], Result[22], Result[23], Result[24], Result[25], Result[26], Result[27], Result[28], Result[29], Result[30], Negative);
  not not_4 (Zero, or_2_out);

  assign Result[31] = Negative;

  // Other names for the same wires on the sheet: R0 = Result[0]; R1 = Result[1]; R2 = Result[2]; R3 = Result[3];
  //   R4 = Result[4]; R5 = Result[5]; R6 = Result[6]; R7 = Result[7]; R8 = Result[8]; R9 = Result[9];
  //   R10 = Result[10]; R11 = Result[11]; R12 = Result[12]; R13 = Result[13]; R14 = Result[14]; R15 = Result[15];
  //   R16 = Result[16]; R17 = Result[17]; R18 = Result[18]; R19 = Result[19]; R20 = Result[20]; R21 = Result[21];
  //   R22 = Result[22]; R23 = Result[23]; R24 = Result[24]; R25 = Result[25]; R26 = Result[26]; R27 = Result[27];
  //   R28 = Result[28]; R29 = Result[29]; R30 = Result[30]; R31 = Negative
endmodule

module Registr (
  input  [31:0] data,
  input  clk,
  input  Reset,
  output [31:0] DataOut
);

  D_Flip_Flop d_ff_1 (.D(data[31]), .clk(clk), .Q(DataOut[31]), .reset(Reset));  // open: Qn, preset
  D_Flip_Flop d_ff_2 (.D(data[30]), .clk(clk), .Q(DataOut[30]), .reset(Reset));  // open: Qn, preset
  D_Flip_Flop d_ff_3 (.D(data[29]), .clk(clk), .Q(DataOut[29]), .reset(Reset));  // open: Qn, preset
  D_Flip_Flop d_ff_4 (.D(data[28]), .clk(clk), .Q(DataOut[28]), .reset(Reset));  // open: Qn, preset
  D_Flip_Flop d_ff_5 (.D(data[27]), .clk(clk), .Q(DataOut[27]), .reset(Reset));  // open: Qn, preset
  D_Flip_Flop d_ff_6 (.D(data[26]), .clk(clk), .Q(DataOut[26]), .reset(Reset));  // open: Qn, preset
  D_Flip_Flop d_ff_7 (.D(data[25]), .clk(clk), .Q(DataOut[25]), .reset(Reset));  // open: Qn, preset
  D_Flip_Flop d_ff_8 (.D(data[24]), .clk(clk), .Q(DataOut[24]), .reset(Reset));  // open: Qn, preset
  D_Flip_Flop d_ff_9 (.D(data[23]), .clk(clk), .Q(DataOut[23]), .reset(Reset));  // open: Qn, preset
  D_Flip_Flop d_ff_10 (.D(data[22]), .clk(clk), .Q(DataOut[22]), .reset(Reset));  // open: Qn, preset
  D_Flip_Flop d_ff_11 (.D(data[21]), .clk(clk), .Q(DataOut[21]), .reset(Reset));  // open: Qn, preset
  D_Flip_Flop d_ff_12 (.D(data[20]), .clk(clk), .Q(DataOut[20]), .reset(Reset));  // open: Qn, preset
  D_Flip_Flop d_ff_13 (.D(data[19]), .clk(clk), .Q(DataOut[19]), .reset(Reset));  // open: Qn, preset
  D_Flip_Flop d_ff_14 (.D(data[18]), .clk(clk), .Q(DataOut[18]), .reset(Reset));  // open: Qn, preset
  D_Flip_Flop d_ff_15 (.D(data[17]), .clk(clk), .Q(DataOut[17]), .reset(Reset));  // open: Qn, preset
  D_Flip_Flop d_ff_16 (.D(data[16]), .clk(clk), .Q(DataOut[16]), .reset(Reset));  // open: Qn, preset
  D_Flip_Flop d_ff_17 (.D(data[15]), .clk(clk), .Q(DataOut[15]), .reset(Reset));  // open: Qn, preset
  D_Flip_Flop d_ff_18 (.D(data[14]), .clk(clk), .Q(DataOut[14]), .reset(Reset));  // open: Qn, preset
  D_Flip_Flop d_ff_19 (.D(data[13]), .clk(clk), .Q(DataOut[13]), .reset(Reset));  // open: Qn, preset
  D_Flip_Flop d_ff_20 (.D(data[12]), .clk(clk), .Q(DataOut[12]), .reset(Reset));  // open: Qn, preset
  D_Flip_Flop d_ff_21 (.D(data[11]), .clk(clk), .Q(DataOut[11]), .reset(Reset));  // open: Qn, preset
  D_Flip_Flop d_ff_22 (.D(data[10]), .clk(clk), .Q(DataOut[10]), .reset(Reset));  // open: Qn, preset
  D_Flip_Flop d_ff_23 (.D(data[9]), .clk(clk), .Q(DataOut[9]), .reset(Reset));  // open: Qn, preset
  D_Flip_Flop d_ff_24 (.D(data[8]), .clk(clk), .Q(DataOut[8]), .reset(Reset));  // open: Qn, preset
  D_Flip_Flop d_ff_25 (.D(data[7]), .clk(clk), .Q(DataOut[7]), .reset(Reset));  // open: Qn, preset
  D_Flip_Flop d_ff_26 (.D(data[6]), .clk(clk), .Q(DataOut[6]), .reset(Reset));  // open: Qn, preset
  D_Flip_Flop d_ff_27 (.D(data[5]), .clk(clk), .Q(DataOut[5]), .reset(Reset));  // open: Qn, preset
  D_Flip_Flop d_ff_28 (.D(data[4]), .clk(clk), .Q(DataOut[4]), .reset(Reset));  // open: Qn, preset
  D_Flip_Flop d_ff_29 (.D(data[3]), .clk(clk), .Q(DataOut[3]), .reset(Reset));  // open: Qn, preset
  D_Flip_Flop d_ff_30 (.D(data[2]), .clk(clk), .Q(DataOut[2]), .reset(Reset));  // open: Qn, preset
  D_Flip_Flop d_ff_31 (.D(data[1]), .clk(clk), .Q(DataOut[1]), .reset(Reset));  // open: Qn, preset
  D_Flip_Flop d_ff_32 (.D(data[0]), .clk(clk), .Q(DataOut[0]), .reset(Reset));  // open: Qn, preset
endmodule

module RegisterGroup (
  input  [31:0] Data,
  input  write,
  input  clock,
  input  [4:0] Sel1_ReadReg1,
  input  [4:0] Sel2_ReadReg2,
  input  [4:0] RegNum_WriteReg,
  output [31:0] DataOut1,
  output [31:0] DataOut2
);

  wire and_1_out, and_2_out, and_3_out, and_4_out, and_5_out, and_6_out, and_7_out, and_8_out, and_9_out,
       and_10_out, and_11_out, and_12_out, and_13_out, and_14_out, and_15_out, and_16_out, and_17_out,
       and_18_out, and_19_out, and_20_out, and_21_out, and_22_out, and_23_out, and_24_out, and_25_out,
       and_26_out, and_27_out, and_28_out, and_29_out, and_30_out, and_31_out, and_32_out, decoder_1_out0,
       decoder_1_out1, decoder_1_out2, decoder_1_out3, decoder_1_out4, decoder_1_out5, decoder_1_out6,
       decoder_1_out7, decoder_1_out8, decoder_1_out9, decoder_1_out10, decoder_1_out11, decoder_1_out12,
       decoder_1_out13, decoder_1_out14, decoder_1_out15, decoder_1_out16, decoder_1_out17, decoder_1_out18,
       decoder_1_out19, decoder_1_out20, decoder_1_out21, decoder_1_out22, decoder_1_out23, decoder_1_out24,
       decoder_1_out25, decoder_1_out26, decoder_1_out27, decoder_1_out28, decoder_1_out29, decoder_1_out30,
       decoder_1_out31;
  wire [31:0] registr_1_dataout, registr_2_dataout, registr_3_dataout, registr_4_dataout, registr_5_dataout,
       registr_6_dataout, registr_7_dataout, registr_8_dataout, registr_9_dataout, registr_10_dataout,
       registr_11_dataout, registr_12_dataout, registr_13_dataout, registr_14_dataout, registr_15_dataout,
       registr_16_dataout, registr_17_dataout, registr_18_dataout, registr_19_dataout, registr_20_dataout,
       registr_21_dataout, registr_22_dataout, registr_23_dataout, registr_24_dataout, registr_25_dataout,
       registr_26_dataout, registr_27_dataout, registr_28_dataout, registr_29_dataout, t0_dataout,
       t1_dataout, t2_dataout;

  Decoder #(.enable("false"), .select(5)) decoder_1 (
    .out0(decoder_1_out0), .out1(decoder_1_out1), .out2(decoder_1_out2), .out3(decoder_1_out3),
    .out4(decoder_1_out4), .out5(decoder_1_out5), .out6(decoder_1_out6), .out7(decoder_1_out7),
    .out8(decoder_1_out8), .out9(decoder_1_out9), .out10(decoder_1_out10), .out11(decoder_1_out11),
    .out12(decoder_1_out12), .out13(decoder_1_out13), .out14(decoder_1_out14), .out15(decoder_1_out15),
    .out16(decoder_1_out16), .out17(decoder_1_out17), .out18(decoder_1_out18), .out19(decoder_1_out19),
    .out20(decoder_1_out20), .out21(decoder_1_out21), .out22(decoder_1_out22), .out23(decoder_1_out23),
    .out24(decoder_1_out24), .out25(decoder_1_out25), .out26(decoder_1_out26), .out27(decoder_1_out27),
    .out28(decoder_1_out28), .out29(decoder_1_out29), .out30(decoder_1_out30), .out31(decoder_1_out31),
    .sel(RegNum_WriteReg));
  and and_1 (and_1_out, write, clock, decoder_1_out0);
  and and_2 (and_2_out, write, clock, decoder_1_out1);
  and and_3 (and_3_out, write, clock, decoder_1_out2);
  and and_4 (and_4_out, write, clock, decoder_1_out3);
  and and_5 (and_5_out, write, clock, decoder_1_out4);
  and and_6 (and_6_out, write, clock, decoder_1_out5);
  and and_7 (and_7_out, write, clock, decoder_1_out6);
  and and_8 (and_8_out, write, clock, decoder_1_out7);
  and and_9 (and_9_out, write, clock, decoder_1_out8);
  and and_10 (and_10_out, write, clock, decoder_1_out9);
  and and_11 (and_11_out, write, clock, decoder_1_out10);
  and and_12 (and_12_out, write, clock, decoder_1_out11);
  and and_13 (and_13_out, write, clock, decoder_1_out12);
  and and_14 (and_14_out, write, clock, decoder_1_out13);
  and and_15 (and_15_out, write, clock, decoder_1_out14);
  and and_16 (and_16_out, write, clock, decoder_1_out15);
  and and_17 (and_17_out, write, clock, decoder_1_out16);
  and and_18 (and_18_out, write, clock, decoder_1_out17);
  and and_19 (and_19_out, write, clock, decoder_1_out18);
  and and_20 (and_20_out, write, clock, decoder_1_out19);
  and and_21 (and_21_out, write, clock, decoder_1_out20);
  and and_22 (and_22_out, write, clock, decoder_1_out21);
  and and_23 (and_23_out, write, clock, decoder_1_out22);
  and and_24 (and_24_out, write, clock, decoder_1_out23);
  and and_25 (and_25_out, write, clock, decoder_1_out24);
  and and_26 (and_26_out, write, clock, decoder_1_out25);
  and and_27 (and_27_out, write, clock, decoder_1_out26);
  and and_28 (and_28_out, write, clock, decoder_1_out27);
  and and_29 (and_29_out, write, clock, decoder_1_out28);
  and and_30 (and_30_out, write, clock, decoder_1_out29);
  and and_31 (and_31_out, write, clock, decoder_1_out30);
  and and_32 (and_32_out, write, clock, decoder_1_out31);
  Registr registr_1 (.data(Data), .clk(and_1_out), .DataOut(registr_1_dataout));  // open: Reset
  Registr registr_2 (.data(Data), .clk(and_2_out), .DataOut(registr_2_dataout));  // open: Reset
  Registr registr_3 (.data(Data), .clk(and_3_out), .DataOut(registr_3_dataout));  // open: Reset
  Registr registr_4 (.data(Data), .clk(and_4_out), .DataOut(registr_4_dataout));  // open: Reset
  Registr registr_5 (.data(Data), .clk(and_5_out), .DataOut(registr_5_dataout));  // open: Reset
  Registr registr_6 (.data(Data), .clk(and_6_out), .DataOut(registr_6_dataout));  // open: Reset
  Registr registr_7 (.data(Data), .clk(and_7_out), .DataOut(registr_7_dataout));  // open: Reset
  Registr registr_8 (.data(Data), .clk(and_8_out), .DataOut(registr_8_dataout));  // open: Reset
  Registr t0 (.data(Data), .clk(and_9_out), .DataOut(t0_dataout));  // open: Reset
  Registr t1 (.data(Data), .clk(and_10_out), .DataOut(t1_dataout));  // open: Reset
  Registr t2 (.data(Data), .clk(and_11_out), .DataOut(t2_dataout));  // open: Reset
  Registr registr_9 (.data(Data), .clk(and_12_out), .DataOut(registr_9_dataout));  // open: Reset
  Registr registr_10 (.data(Data), .clk(and_13_out), .DataOut(registr_10_dataout));  // open: Reset
  Registr registr_11 (.data(Data), .clk(and_14_out), .DataOut(registr_11_dataout));  // open: Reset
  Registr registr_12 (.data(Data), .clk(and_15_out), .DataOut(registr_12_dataout));  // open: Reset
  Registr registr_13 (.data(Data), .clk(and_16_out), .DataOut(registr_13_dataout));  // open: Reset
  Registr registr_14 (.data(Data), .clk(and_17_out), .DataOut(registr_14_dataout));  // open: Reset
  Registr registr_15 (.data(Data), .clk(and_18_out), .DataOut(registr_15_dataout));  // open: Reset
  Registr registr_16 (.data(Data), .clk(and_19_out), .DataOut(registr_16_dataout));  // open: Reset
  Registr registr_17 (.data(Data), .clk(and_20_out), .DataOut(registr_17_dataout));  // open: Reset
  Registr registr_18 (.data(Data), .clk(and_21_out), .DataOut(registr_18_dataout));  // open: Reset
  Registr registr_19 (.data(Data), .clk(and_22_out), .DataOut(registr_19_dataout));  // open: Reset
  Registr registr_20 (.data(Data), .clk(and_23_out), .DataOut(registr_20_dataout));  // open: Reset
  Registr registr_21 (.data(Data), .clk(and_24_out), .DataOut(registr_21_dataout));  // open: Reset
  Registr registr_22 (.data(Data), .clk(and_25_out), .DataOut(registr_22_dataout));  // open: Reset
  Registr registr_23 (.data(Data), .clk(and_26_out), .DataOut(registr_23_dataout));  // open: Reset
  Registr registr_24 (.data(Data), .clk(and_27_out), .DataOut(registr_24_dataout));  // open: Reset
  Registr registr_25 (.data(Data), .clk(and_28_out), .DataOut(registr_25_dataout));  // open: Reset
  Registr registr_26 (.data(Data), .clk(and_29_out), .DataOut(registr_26_dataout));  // open: Reset
  Registr registr_27 (.data(Data), .clk(and_30_out), .DataOut(registr_27_dataout));  // open: Reset
  Registr registr_28 (.data(Data), .clk(and_31_out), .DataOut(registr_28_dataout));  // open: Reset
  Registr registr_29 (.data(Data), .clk(and_32_out), .DataOut(registr_29_dataout));  // open: Reset
  Multiplexer #(.select(5), .width(32)) multiplexer_1 (
    .in0(registr_1_dataout), .in1(registr_2_dataout), .in2(registr_3_dataout), .in3(registr_4_dataout),
    .in4(registr_5_dataout), .in5(registr_6_dataout), .in6(registr_7_dataout), .in7(registr_8_dataout),
    .in8(t0_dataout), .in9(t1_dataout), .in10(t2_dataout), .in11(registr_9_dataout),
    .in12(registr_10_dataout), .in13(registr_11_dataout), .in14(registr_12_dataout),
    .in15(registr_13_dataout), .in16(registr_14_dataout), .in17(registr_15_dataout),
    .in18(registr_16_dataout), .in19(registr_17_dataout), .in20(registr_18_dataout),
    .in21(registr_19_dataout), .in22(registr_20_dataout), .in23(registr_21_dataout),
    .in24(registr_22_dataout), .in25(registr_23_dataout), .in26(registr_24_dataout),
    .in27(registr_25_dataout), .in28(registr_26_dataout), .in29(registr_27_dataout),
    .in30(registr_28_dataout), .in31(registr_29_dataout), .out(DataOut1), .sel(Sel1_ReadReg1));
  Multiplexer #(.select(5), .width(32)) multiplexer_2 (
    .in0(registr_1_dataout), .in1(registr_2_dataout), .in2(registr_3_dataout), .in3(registr_4_dataout),
    .in4(registr_5_dataout), .in5(registr_6_dataout), .in6(registr_7_dataout), .in7(registr_8_dataout),
    .in8(t0_dataout), .in9(t1_dataout), .in10(t2_dataout), .in11(registr_9_dataout),
    .in12(registr_10_dataout), .in13(registr_11_dataout), .in14(registr_12_dataout),
    .in15(registr_13_dataout), .in16(registr_14_dataout), .in17(registr_15_dataout),
    .in18(registr_16_dataout), .in19(registr_17_dataout), .in20(registr_18_dataout),
    .in21(registr_19_dataout), .in22(registr_20_dataout), .in23(registr_21_dataout),
    .in24(registr_22_dataout), .in25(registr_23_dataout), .in26(registr_24_dataout),
    .in27(registr_25_dataout), .in28(registr_26_dataout), .in29(registr_27_dataout),
    .in30(registr_28_dataout), .in31(registr_29_dataout), .out(DataOut2), .sel(Sel2_ReadReg2));
endmodule

module ControlUnit (
  input  Op5,
  input  Op4,
  input  Op3,
  input  Op2,
  input  Op1,
  input  Op0,
  output RegDst,
  output ALUSrc,
  output MemtoReg,
  output RegWrite,
  output MemRead,
  output MemWrite,
  output Branch,
  output ALUOp1,
  output ALUOp0,
  output Jump
);

  and Jmp (Jump, ~Op5, ~Op4, ~Op3, ~Op2, Op1, ~Op0);  // AND_Gate
  and R_format (ALUOp1, ~Op5, ~Op4, ~Op3, ~Op2, ~Op1, ~Op0);  // AND_Gate
  and lw (MemRead, Op5, ~Op4, ~Op3, ~Op2, Op1, Op0);  // AND_Gate
  and sw (MemWrite, Op5, ~Op4, Op3, ~Op2, Op1, Op0);  // AND_Gate
  and beq (ALUOp0, ~Op5, ~Op4, ~Op3, Op2, ~Op1, ~Op0);  // AND_Gate
  or or_1 (ALUSrc, MemRead, MemWrite);
  or or_2 (RegWrite, ALUOp1, MemRead);

  assign Branch = ALUOp0;
  assign MemtoReg = MemRead;
  assign RegDst = ALUOp1;
endmodule

module ALUControl (
  input  [5:0] FUNCT,
  input  OP1,
  input  OP2,
  output [3:0] out_4
);

  wire and_1_out, and_2_out, and_3_out, and_4_out, and_5_out, and_6_out, and_7_out, and_8_out, and_9_out,
       and_10_out;

  and and_1 (and_1_out, ~OP1, OP2);  // AND_Gate
  and and_2 (and_2_out, OP1, ~OP2, FUNCT[5], ~FUNCT[4], ~FUNCT[3], ~FUNCT[2], FUNCT[1], ~FUNCT[0]);  // AND_Gate
  and and_3 (and_3_out, OP1, ~OP2, FUNCT[5], ~FUNCT[4], FUNCT[3], ~FUNCT[2], FUNCT[1], ~FUNCT[0]);  // AND_Gate
  and and_4 (and_4_out, ~OP1, ~OP2);  // AND_Gate
  and and_5 (and_5_out, ~OP1, OP2);  // AND_Gate
  and and_6 (and_6_out, OP1, ~OP2, FUNCT[5], ~FUNCT[4], ~FUNCT[3], ~FUNCT[2], ~FUNCT[1], ~FUNCT[0]);  // AND_Gate
  and and_7 (and_7_out, OP1, ~OP2, FUNCT[5], ~FUNCT[4], ~FUNCT[3], ~FUNCT[2], FUNCT[1], ~FUNCT[0]);  // AND_Gate
  and and_8 (and_8_out, OP1, ~OP2, FUNCT[5], ~FUNCT[4], FUNCT[3], ~FUNCT[2], FUNCT[1], ~FUNCT[0]);  // AND_Gate
  and and_9 (and_9_out, OP1, ~OP2, FUNCT[5], ~FUNCT[4], ~FUNCT[3], FUNCT[2], ~FUNCT[1], FUNCT[0]);  // AND_Gate
  and and_10 (and_10_out, OP1, ~OP2, FUNCT[5], ~FUNCT[4], FUNCT[3], ~FUNCT[2], FUNCT[1], ~FUNCT[0]);  // AND_Gate
  or A (out_4[3], 1'b0, 1'b0);
  or B (out_4[2], and_1_out, and_2_out, and_3_out);
  or C (out_4[1], and_4_out, and_5_out, and_6_out, and_7_out, and_8_out);
  or D (out_4[0], and_9_out, and_10_out);
endmodule
